// Logisim project ETHEL.circ as structural Verilog: 3 circuits, main circuit main
module main (
);

  wire alu_1_z_flag, and_1_out, not_1_out, not_2_out, not_3_out, RAM_CLOCK_out, SYS_CLOCK1_out;
  wire [1:1] or_1_out;
  wire [2:0] multiplexer_3_out;
  wire [7:0] alu_1_aluout, alu_1_aluout_2, alu_1_aluout_3, alu_1_aluout_4, alu_1_aluout_5, alu_1_aluout_6,
       alu_1_aluout_7, alu_1_aluout_8;
  wire [15:0] adder_1_out, adder_2_out, multiplexer_1_out, PROGRAM_COUNTER_q;
  wire [31:0] INSTRUCTION_MEMORY_dout;
  wire [63:0] bit_extender_1_out, bit_extender_2_out, DRAM_dout, multiplexer_2_out, multiplexer_4_out,
       REGISTERS_regdata1, REGISTERS_regdata2;

  Clock #(.highDuration(4), .lowDuration(4)) SYS_CLOCK1 (.out(SYS_CLOCK1_out));
  Multiplexer #(.select(2), .width(16)) multiplexer_1 (
    .in0(adder_1_out), .in1({alu_1_aluout_2, alu_1_aluout}), .in2(adder_2_out), .out(multiplexer_1_out),
    .sel({or_1_out[1], INSTRUCTION_MEMORY_dout[20]}));  // open: in3
  Clock RAM_CLOCK (.out(RAM_CLOCK_out));
  or or_1 (or_1_out[1], and_1_out, INSTRUCTION_MEMORY_dout[22]);
  not not_1 (not_1_out, SYS_CLOCK1_out);
  and and_1 (and_1_out, INSTRUCTION_MEMORY_dout[21], alu_1_z_flag);
  assign bit_extender_1_out = {{48{adder_1_out[15]}}, adder_1_out};  // Bit_Extender bit_extender_1
  not not_2 (not_2_out, not_1_out);
  Adder #(.width(16)) adder_1 (.a(PROGRAM_COUNTER_q), .b(16'h1), .out(adder_1_out));  // open: cin, cout
  Adder #(.width(16)) adder_2 (
    .a(PROGRAM_COUNTER_q), .b(INSTRUCTION_MEMORY_dout[18:3]), .out(adder_2_out));  // open: cin, cout
  assign bit_extender_2_out = {{48{INSTRUCTION_MEMORY_dout[18]}}, INSTRUCTION_MEMORY_dout[18:3]};  // Bit_Extender bit_extender_2
  not not_3 (not_3_out, not_2_out);
  RAM #(.addrWidth(16), .dataWidth(32)) INSTRUCTION_MEMORY (
    .addr(PROGRAM_COUNTER_q), .we(1'b0), .oe(1'b1), .clk(SYS_CLOCK1_out), .dout(INSTRUCTION_MEMORY_dout));  // open: din
  Register #(.width(16)) PROGRAM_COUNTER (
    .D(multiplexer_1_out), .en(not_3_out), .clk(not_3_out), .Q(PROGRAM_COUNTER_q));  // open: clr
  register_file REGISTERS (
    .ReadReg1(INSTRUCTION_MEMORY_dout[5:3]), .ReadReg2(INSTRUCTION_MEMORY_dout[2:0]),
    .WriteReg(multiplexer_3_out), .RegDataW(multiplexer_4_out), .RegWrite(INSTRUCTION_MEMORY_dout[28]),
    .Clock(SYS_CLOCK1_out), .RegData1(REGISTERS_regdata1), .RegData2(REGISTERS_regdata2));
  ALU alu_1 (
    .INPUTA(REGISTERS_regdata1), .INPUTB(multiplexer_2_out), .ALUop(INSTRUCTION_MEMORY_dout[31:30]),
    .ALUout({alu_1_aluout_8, alu_1_aluout_7, alu_1_aluout_6, alu_1_aluout_5, alu_1_aluout_4, alu_1_aluout_3, alu_1_aluout_2, alu_1_aluout}),
    .Z_FLAG(alu_1_z_flag));
  Multiplexer #(.width(64)) multiplexer_2 (
    .in0(REGISTERS_regdata2), .in1(bit_extender_2_out), .out(multiplexer_2_out),
    .sel(INSTRUCTION_MEMORY_dout[29]));
  RAM #(.dataWidth(64)) DRAM (
    .addr(alu_1_aluout), .we(INSTRUCTION_MEMORY_dout[26]), .oe(INSTRUCTION_MEMORY_dout[25]),
    .clk(RAM_CLOCK_out), .din(multiplexer_2_out), .dout(DRAM_dout));
  Multiplexer #(.width(3)) multiplexer_3 (
    .in0(INSTRUCTION_MEMORY_dout[2:0]), .in1(INSTRUCTION_MEMORY_dout[8:6]), .out(multiplexer_3_out),
    .sel(INSTRUCTION_MEMORY_dout[27]));
  Multiplexer #(.select(2), .width(64)) multiplexer_4 (
    .in0({alu_1_aluout_8, alu_1_aluout_7, alu_1_aluout_6, alu_1_aluout_5, alu_1_aluout_4, alu_1_aluout_3, alu_1_aluout_2, alu_1_aluout}),
    .in1(bit_extender_1_out), .in2(DRAM_dout), .out(multiplexer_4_out), .sel(INSTRUCTION_MEMORY_dout[24:23]));  // open: in3

  // Notes on the sheet:
  //   E.T.H.E.L. CPU by Joshua Bernstein
  //   I pledge my honor that I have abided by the Stevens Honor System.
  //   Instruction Memory
  //   Data Memory
endmodule

module register_file (
  input  [2:0] ReadReg1,
  input  [2:0] ReadReg2,
  input  [2:0] WriteReg,
  input  [63:0] RegDataW,
  input  RegWrite,
  input  Clock,
  output [63:0] RegData1,
  output [63:0] RegData2
);

  wire and_1_out, and_2_out, and_3_out, and_4_out, AND_OF_0DECODE_AND_REGWRITE_out,
       AND_OF_1DECODE_AND_REGWRITE_out, AND_OF_2DECODE_AND_REGWRITE_out, AND_OF_3DECODE_AND_REGWRITE_out,
       decoder_1_out0, decoder_1_out1, decoder_1_out2, decoder_1_out3, decoder_1_out4, decoder_1_out5,
       decoder_1_out6, decoder_1_out7, not_1_out, not_2_out, not_3_out;
  wire [63:0] E0_q, E1_q, E2_q, E3_q, E4_q, E5_q, E6_q, E7_q;

  Decoder #(.select(3)) decoder_1 (
    .out0(decoder_1_out0), .out1(decoder_1_out1), .out2(decoder_1_out2), .out3(decoder_1_out3),
    .out4(decoder_1_out4), .out5(decoder_1_out5), .out6(decoder_1_out6), .out7(decoder_1_out7), .sel(WriteReg));  // open: en
  not not_1 (not_1_out, Clock);
  not not_2 (not_2_out, not_1_out);
  not not_3 (not_3_out, not_2_out);
  and AND_OF_0DECODE_AND_REGWRITE (AND_OF_0DECODE_AND_REGWRITE_out, decoder_1_out0, RegWrite);
  and AND_OF_1DECODE_AND_REGWRITE (AND_OF_1DECODE_AND_REGWRITE_out, decoder_1_out1, RegWrite);
  and AND_OF_2DECODE_AND_REGWRITE (AND_OF_2DECODE_AND_REGWRITE_out, RegWrite, decoder_1_out2);
  and AND_OF_3DECODE_AND_REGWRITE (AND_OF_3DECODE_AND_REGWRITE_out, decoder_1_out3, RegWrite);
  and and_1 (and_1_out, decoder_1_out4, RegWrite);
  and and_2 (and_2_out, decoder_1_out5, RegWrite);
  and and_3 (and_3_out, RegWrite, decoder_1_out6);
  and and_4 (and_4_out, decoder_1_out7, RegWrite);
  Register #(.width(64)) E0 (
    .D(RegDataW), .en(AND_OF_0DECODE_AND_REGWRITE_out), .clk(not_3_out), .Q(E0_q));  // open: clr
  Register #(.width(64)) E1 (
    .D(RegDataW), .en(AND_OF_1DECODE_AND_REGWRITE_out), .clk(not_3_out), .Q(E1_q));  // open: clr
  Register #(.width(64)) E2 (
    .D(RegDataW), .en(AND_OF_2DECODE_AND_REGWRITE_out), .clk(not_3_out), .Q(E2_q));  // open: clr
  Register #(.width(64)) E3 (
    .D(RegDataW), .en(AND_OF_3DECODE_AND_REGWRITE_out), .clk(not_3_out), .Q(E3_q));  // open: clr
  Register #(.width(64)) E4 (.D(RegDataW), .en(and_1_out), .clk(not_3_out), .Q(E4_q));  // open: clr
  Register #(.width(64)) E5 (.D(RegDataW), .en(and_2_out), .clk(not_3_out), .Q(E5_q));  // open: clr
  Register #(.width(64)) E6 (.D(RegDataW), .en(and_3_out), .clk(not_3_out), .Q(E6_q));  // open: clr
  Register #(.width(64)) E7 (.D(RegDataW), .en(and_4_out), .clk(not_3_out), .Q(E7_q));  // open: clr
  Multiplexer #(.select(3), .width(64)) multiplexer_1 (
    .in0(E0_q), .in1(E1_q), .in2(E2_q), .in3(E3_q), .in4(E4_q), .in5(E5_q), .in6(E6_q), .in7(E7_q),
    .out(RegData1), .sel(ReadReg1));
  Multiplexer #(.select(3), .width(64)) multiplexer_2 (
    .in0(E0_q), .in1(E1_q), .in2(E2_q), .in3(E3_q), .in4(E4_q), .in5(E5_q), .in6(E6_q), .in7(E7_q),
    .out(RegData2), .sel(ReadReg2));
endmodule

module ALU (
  input  [63:0] INPUTA,
  input  [63:0] INPUTB,
  input  [1:0] ALUop,
  output [63:0] ALUout,
  output Z_FLAG
);

  wire or_1_out;
  wire [63:0] adder_1_out, subtractor_1_out;

  Adder #(.width(64)) adder_1 (.a(INPUTA), .b(INPUTB), .out(adder_1_out));  // open: cin, cout
  Subtractor #(.width(64)) subtractor_1 (.a(INPUTA), .b(INPUTB), .out(subtractor_1_out));  // open: bin, bout
  Multiplexer #(.select(2), .width(64)) multiplexer_1 (
    .in0(INPUTB), .in1(adder_1_out), .in2(INPUTA), .in3(subtractor_1_out), .out(ALUout), .sel(ALUop));
  or or_1 (or_1_out, ALUout[0], ALUout[1], ALUout[2], ALUout[3], ALUout[4], ALUout[5], ALUout[6], ALUout[7], ALUout[8], ALUout[9], ALUout[10], ALUout[11], ALUout[12], ALUout[13], ALUout[14], ALUout[15], ALUout[16], ALUout[17], ALUout[18], ALUout[19], ALUout[20], ALUout[21], ALUout[22], ALUout[23], ALUout[24], ALUout[25], ALUout[26], ALUout[27], ALUout[28], ALUout[29], ALUout[30], ALUout[31], ALUout[32], ALUout[33], ALUout[34], ALUout[35], ALUout[36], ALUout[37], ALUout[38], ALUout[39], ALUout[40], ALUout[41], ALUout[42], ALUout[43], ALUout[44], ALUout[45], ALUout[46], ALUout[47], ALUout[48], ALUout[49], ALUout[50], ALUout[51], ALUout[52], ALUout[53], ALUout[54], ALUout[55], ALUout[56], ALUout[57], ALUout[58], ALUout[59], ALUout[60], ALUout[61], ALUout[62], ALUout[63]);
  not not_1 (Z_FLAG, or_1_out);
endmodule
